# Fritzing sketch chanber_controller Sketch (saved by Fritzing 0.9.9b)
breadboards: 1

parts:
  Grove1 = Grove OLED 128x96
  Part1 = Arduino Nano (Rev3.0) (ICSP)
  S1 = Pushbutton [package="[THT]"]
  S2 = Pushbutton [package="[THT]"]
  S3 = Pushbutton [package="[THT]"]
  DHT1 = DHT22 Humidity and Temperature Sensor
  R1 = Resistor [tolerance=±5% resistance=220 package="0603 [SMD]"]
  R2 = Resistor [tolerance=±5% resistance=220 package="0603 [SMD]"]
  R3 = Resistor [tolerance=±5% resistance=220 package="0603 [SMD]"]
  LED1 = LED - 5mm [color="Red (633nm)" current=0.030 package="5 mm [THT]"]
  LED2 = LED - 5mm [color="Red (633nm)" current=0.030 package="5 mm [THT]"]
  LED3 = LED - 5mm [color="Red (633nm)" current=0.030 package="5 mm [THT]"]

nets:
  GND: Grove1.GND, Part1.GND, DHT1.GND, R1.Pin_1, R2.Pin_1, R3.Pin_1
  VCC: Grove1.VCC, Part1.5V, S1.Pin_1, S1.Pin_2, S2.Pin_1, S2.Pin_2, S3.Pin_1, S3.Pin_2, DHT1.VDD
  N1: Grove1.SDA, Part1.A5
  N2: Grove1.SCL, Part1.A6
  N3: Part1.D2, S1.Pin_3, S1.Pin_4
  N4: Part1.D3, S2.Pin_3, S2.Pin_4
  N5: Part1.D4, S3.Pin_3, S3.Pin_4
  N6: Part1.D6, DHT1.DATA
  N7: Part1.A2, LED3.cathode
  N8: Part1.A1, LED2.cathode
  N9: Part1.A0, LED1.cathode
  N10: R1.Pin_0, LED1.anode
  N11: R2.Pin_0, LED2.anode
  N12: R3.Pin_0, LED3.anode
