# Fritzing sketch chanber_controller Sketch_m3 (saved by Fritzing 0.9.9b)
perfboards: 2

parts:
  Grove1 = Grove OLED 128x96
  DHT1 = DHT22 Humidity and Temperature Sensor
  Fan_PWM = LED - 5mm [color="Red (633nm)" current=0.030 package="5 mm [THT]"]
  Vents = LED - 5mm [color="Red (633nm)" current=0.030 package="5 mm [THT]"]
  Lights = LED - 5mm [color="Red (633nm)" current=0.030 package="5 mm [THT]"]
  PB_Lights = Pushbutton [package="[SMD]"]
  R4 = Resistor [tolerance=±5% resistance=1k package="0805 [SMD]"]
  R5 = Resistor [tolerance=±5% resistance=1k package="0805 [SMD]"]
  R6 = Resistor [tolerance=±5% resistance=1k package="0805 [SMD]"]
  J1 = male pin header, 3 pins [form="♂ (male)"]
  PB_Fans = Pushbutton [package="[SMD]"]
  PB_Vents = Pushbutton [package="[SMD]"]
  J2 = Screw terminal - 2 pins [package=THT]
  C1 = Electrolytic Capacitor [capacitance=1µF voltage=35V package="100 mil [THT, electrolytic]"]  # not connected
  C2 = Electrolytic Capacitor [capacitance=1µF voltage=35V package="100 mil [THT, electrolytic]"]  # not connected
  U2 = Voltage Regulator - 5V [package="TO220 [THT]"]  # not connected
  J3 = molex pin header, 1 pin [form=molex]
  VCC1 = Battery block 9V
  R7 = Resistor [tolerance=±5% resistance=220 package="0805 [SMD]"]
  R8 = Resistor [tolerance=±5% resistance=220 package="0805 [SMD]"]
  R9 = Resistor [tolerance=±5% resistance=220 package="0805 [SMD]"]
  J4 = male pin header, 2 pins [form="♂ (male)"]
  J5 = male pin header, 2 pins [form="♂ (male)"]
  J6 = male pin header, 2 pins [form="♂ (male)"]
  J7 = male pin header, 4 pins [form="♂ (male)"]
  J8 = male pin header, 3 pins [form="♂ (male)"]
  J9 = male pin header, 4 pins [form="♂ (male)"]
  J10 = male pin header, 4 pins [form="♂ (male)"]
  R10 = Rotary Potentiometer (Small) [maximum_resistance=100kΩ package=THT]
  J11 = male alternating pin header, 3 pins [form="♂ (male)"]
  J12 = female pin header, 3 pins [form="♀ (female)"]
  J13 = female pin header, 4 pins [form="♀ (female)"]
  J14 = female pin header, 3 pins [form="♀ (female)"]
  Q1 = Basic FET N-Channel [package="TO220 [THT]"]
  R11 = Resistor [tolerance=±5% resistance=1k package="0805 [SMD]"]
  J15 = male alternating pin header, 2 pins [form="♂ (male)"]
  J16 = female pin header, 2 pins [form="♀ (female)"]
  M1 = DC Motor
  D1 = Rectifier Diode [part_number=1N4001 package="300 mil [THT]"]
  U3 = ATTiny84 [package=dip]  # not connected
  Driver2 = 28BYJ-48 Driver Module [part_number=ULN2003 package=THT]
  SM2 = 28BYJ-48 Stepper Motor [part_number=28BYJ-48]
  Mod1 = YL-99 Limit switch and LED  # not connected
  Mod2 = Raspberry Pi Pico  # not connected

nets:
  GND: Grove1.GND, DHT1.GND, J7.pin4, J8.pin3, J9.pin4, J10.pin4, J12.pin3, J13.pin4
  VCC: Grove1.VCC, DHT1.VDD, J7.pin3, J8.pin2, J9.pin3, J10.pin3, J12.pin2, J13.pin3
  N1: Grove1.SDA, J7.pin2, J9.pin2, J10.pin2, J13.pin2
  N2: Grove1.SCL, J7.pin1, J9.pin1, J10.pin1, J13.pin1
  N3: DHT1.DATA, J8.pin1, J12.pin1
  N4: Fan_PWM.cathode, J6.pin2
  N5: Fan_PWM.anode, R9.Pin_0, J6.pin1
  N6: Vents.cathode, J5.pin2
  N7: Vents.anode, R8.Pin_0, J5.pin1
  N8: Lights.cathode, J4.pin2
  N9: Lights.anode, R7.Pin_0, J4.pin1
  N10: PB_Lights.Pin_1, PB_Lights.Pin_2, R4.Pin_1, J1.pin1
  N11: PB_Lights.Pin_3, PB_Lights.Pin_4, PB_Fans.Pin_3, PB_Fans.Pin_4, PB_Vents.Pin_3, PB_Vents.Pin_4, J3.pin1
  N12: R4.Pin_0, R5.Pin_0, R6.Pin_0, R7.Pin_1, R8.Pin_1, R9.Pin_1
  N13: R5.Pin_1, J1.pin2, PB_Vents.Pin_1, PB_Vents.Pin_2
  N14: R6.Pin_1, J1.pin3, PB_Fans.Pin_1, PB_Fans.Pin_2
  N15: J2.pin1, VCC1.+, J15.pin2, J16.pin2, M1.pin_2, D1.cathode
  N16: J2.pin2, VCC1.-, R10.leg1, J11.pin1, J14.pin1, Q1.source, R11.Pin_0
  N17: R10.wiper, J11.pin2, J14.pin2
  N18: R10.leg2, J11.pin3, J14.pin3
  N19: Q1.gate, R11.Pin_1
  N20: Q1.drain, J15.pin1, J16.pin1, M1.pin_1, D1.anode
  N21: Driver2.blue-pin, SM2.blue-pin
  N22: Driver2.pink-pin, SM2.pink-pin
  N23: Driver2.yellow-pin, SM2.yellow-pin
  N24: Driver2.orange-pin, SM2.orange-pin
  N25: Driver2.red-pin, SM2.red-pin

custom parts:
  ATTiny84: Atmel ATTiny84 processor. 8 ADC pins, 4 PWM pins. Available in either 10MHz or 20MHz. The last 2 pin numbers refer to arduino. D6 = Arduino 6, A6 = Arduino A6 example: PA6 (SDA/MOSI/OC1A/DI/AD6/PCINT6/D6/A6) NOTE: This part is diagrammed to suit the MIT HLT ATTiny84 core at https://github.com/damellis/attiny/
  28BYJ-48 Driver Module: ULN2003 Driver Module for the 28BYJ-48 Unipolar Stepper Motor LED A - Blue wire - Bottom coil left LED B - Pink wire - Top coil left LED C - Yellow wire - Bottom coil right LED D - Orange wire - Top coil right Common rail - red Connector pins: blue - pink - yellow - orange - red Control pins - IN1 to IN4 Power pins - GND & Vmotor (5-12V) On/Off jumper (if removed, power to motor is cut).
  28BYJ-48 Stepper Motor: Unipolar Stepper Motor 28BYJ-48 Top coil - pink & orange Bottom coil - blue & yellow Common rail - red Connector pins: blue - pink - yellow - orange - red
  Raspberry Pi Pico: Raspberry Pi Pico. Based around the RP2040 microcontroller the Pico is a low cost microcontroller device bringing Raspberry Pi quality, cost, and easy of use to the microcontroller space. Jan 2021, Split part in to two versions: tht (this one) and SMD. This one will drill holes for a .1 in header in pcb to allow plugging in the module as well as providing pads to solder the module to the top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
